// Logisim project ALU.circ as structural Verilog
module Logic_Unit (
  input  [7:0] A,
  input  [7:0] B,
  input  [2:0] in_3,
  output out_4,
  output out_5,
  output [7:0] out_6
);

  wire [7:0] adder_1_out, and_1_out, not_1_out, not_2_out, or_1_out, subtractor_1_out, xor_1_out;

  Adder adder_1 (.a(B), .b(A), .out(adder_1_out), .cout(out_4));  // open: cin
  Subtractor subtractor_1 (.a(B), .b(A), .out(subtractor_1_out), .bout(out_5));  // open: bin
  assign and_1_out = B & A;  // AND_Gate and_1, 8 bits wide
  assign or_1_out = B | A;  // OR_Gate or_1, 8 bits wide
  assign xor_1_out = B ^ A;  // XOR_Gate xor_1, 8 bits wide
  assign not_1_out = ~A;  // NOT_Gate not_1, 8 bits wide
  assign not_2_out = ~B;  // NOT_Gate not_2, 8 bits wide
  Multiplexer #(.disabled("Z"), .select(3), .width(8)) multiplexer_1 (
    .in0({8{1'b0}}), .in1({8{1'b0}}), .in2(adder_1_out), .in3(subtractor_1_out), .in4(and_1_out),
    .in5(or_1_out), .in6(xor_1_out), .in7(not_1_out), .out(out_6), .sel(in_3));
endmodule
